// Logisim project Circuit.circ as structural Verilog: 2 circuits, main circuit main
module main (
  input  [15:0] A,
  input  [15:0] B,
  input  [15:0] C,
  input  [4:0] OPT,
  output [15:0] A_2,
  output Overflow,
  output Divide_by_0,
  output Branch
);

  wire adder_1_cout, comparator_1_eq, comparator_2_eq, comparator_3_lt, comparator_4_eq, comparator_4_lt,
       comparator_5_eq, comparator_6_eq, comparator_7_lt, comparator_8_eq, comparator_9_eq, comparator_10_gt,
       multiplexer_8_out, multiplexer_9_out, multiplexer_11_out, multiplexer_12_out, not_2_out, not_3_out,
       or_2_out, subtractor_1_bout;
  wire [15:0] adder_1_out, and_1_out, divider_1_out, divider_2_rem, multiplexer_1_out, multiplexer_2_out,
       multiplexer_3_out, multiplexer_4_out, multiplexer_5_out, multiplexer_6_out, multiplier_1_out,
       not_1_out, or_1_out, subtractor_1_out, undriven, undriven_2, xor_1_out;

  Adder #(.width(16)) adder_1 (.a(A), .b(B), .out(adder_1_out), .cout(adder_1_cout));  // open: cin
  Subtractor #(.width(16)) subtractor_1 (.a(A), .b(B), .out(subtractor_1_out), .bout(subtractor_1_bout));  // open: bin
  Multiplier #(.width(16)) multiplier_1 (.a(A), .b(B), .out(multiplier_1_out));  // open: cin, cout
  Divider #(.width(16)) divider_1 (.a(A), .b(B), .out(divider_1_out));  // open: upper, rem
  Divider #(.width(16)) divider_2 (.a(A), .b(B), .rem(divider_2_rem));  // open: out, upper
  assign not_1_out = ~A;  // NOT_Gate not_1, 16 bits wide
  ShiftLeft shiftleft_1 (.A(A), .B(B), .OUTPUT(undriven));
  ShiftLeft shiftleft_2 (.A(A), .B(B), .OUTPUT(undriven_2));
  Comparator #(.width(16)) comparator_1 (.a(A), .b(B), .eq(comparator_1_eq));  // open: gt, lt
  Comparator #(.width(16)) comparator_2 (.a(A), .b(B), .eq(comparator_2_eq));  // open: gt, lt
  Comparator #(.width(16)) comparator_3 (.a(A), .b(B), .lt(comparator_3_lt));  // open: gt, eq
  Comparator #(.width(16)) comparator_4 (.a(A), .b(B), .eq(comparator_4_eq), .lt(comparator_4_lt));  // open: gt
  Comparator #(.width(16)) comparator_5 (.a(A), .b({16{1'b0}}), .eq(comparator_5_eq));  // open: gt, lt
  Comparator #(.width(16)) comparator_6 (.a(A), .b({16{1'b0}}), .eq(comparator_6_eq));  // open: gt, lt
  assign and_1_out = A & B;  // AND_Gate and_1, 16 bits wide
  assign or_1_out = A | B;  // OR_Gate or_1, 16 bits wide
  assign xor_1_out = A ^ B;  // XOR_Gate xor_1, 16 bits wide
  not not_2 (not_2_out, comparator_2_eq);
  or or_2 (or_2_out, comparator_4_eq, comparator_4_lt);
  not not_3 (not_3_out, comparator_6_eq);
  Multiplexer #(.width(16)) multiplexer_1 (
    .in0({16{1'b0}}), .in1(C), .out(multiplexer_1_out), .sel(comparator_1_eq));  // open: en
  Multiplexer #(.width(16)) multiplexer_2 (
    .in0({16{1'b0}}), .in1(C), .out(multiplexer_2_out), .sel(not_2_out));  // open: en
  Multiplexer #(.width(16)) multiplexer_3 (
    .in0({16{1'b0}}), .in1(C), .out(multiplexer_3_out), .sel(comparator_3_lt));  // open: en
  Multiplexer #(.width(16)) multiplexer_4 (
    .in0({16{1'b0}}), .in1(C), .out(multiplexer_4_out), .sel(or_2_out));  // open: en
  Multiplexer #(.width(16)) multiplexer_5 (
    .in0({16{1'b0}}), .in1(C), .out(multiplexer_5_out), .sel(comparator_5_eq));  // open: en
  Multiplexer #(.width(16)) multiplexer_6 (
    .in0({16{1'b0}}), .in1(C), .out(multiplexer_6_out), .sel(not_3_out));  // open: en
  Multiplexer #(.select(5), .width(16)) multiplexer_7 (
    .in0(adder_1_out), .in1(subtractor_1_out), .in2(multiplier_1_out), .in3(divider_1_out),
    .in4(divider_2_rem), .in5(and_1_out), .in6(or_1_out), .in7(xor_1_out), .in8(not_1_out), .in9(undriven),
    .in10(undriven_2), .in16(multiplexer_1_out), .in17(multiplexer_2_out), .in18(multiplexer_3_out),
    .in19(multiplexer_4_out), .in20(multiplexer_5_out), .in21(multiplexer_6_out), .out(A_2), .sel(OPT));  // open: in11, in12, in13, in14, in15, in22, in23, in24, in25, in26, in27, in28, in29, in30, in31, en
  Comparator #(.width(5), .mode("unsigned")) comparator_7 (
    .a(OPT), .b(5'b00011), .lt(comparator_7_lt));  // open: gt, eq
  Comparator #(.width(5), .mode("unsigned")) comparator_8 (
    .a(OPT), .b(5'b00011), .eq(comparator_8_eq));  // open: gt, lt
  Comparator #(.width(5), .mode("unsigned")) comparator_9 (
    .a(OPT), .b(5'b00100), .eq(comparator_9_eq));  // open: gt, lt
  Comparator #(.width(5), .mode("unsigned")) comparator_10 (
    .a(OPT), .b(5'b01010), .gt(comparator_10_gt));  // open: eq, lt
  Multiplexer #(.select(2)) multiplexer_8 (
    .in0(adder_1_cout), .in1(subtractor_1_bout), .in2(1'b0), .out(multiplexer_8_out), .sel(OPT[1:0]));  // open: in3, en
  Multiplexer #(.select(3)) multiplexer_9 (
    .in0(comparator_1_eq), .in1(not_2_out), .in2(comparator_3_lt), .in3(or_2_out), .in4(comparator_5_eq),
    .in5(not_3_out), .out(multiplexer_9_out), .sel(OPT[2:0]));  // open: in6, in7, en
  Multiplexer multiplexer_10 (.in0(1'b0), .in1(multiplexer_8_out), .out(Overflow), .sel(comparator_7_lt));  // open: en
  Multiplexer multiplexer_11 (.in0(1'b0), .in1(1'b0), .out(multiplexer_11_out), .sel(comparator_8_eq));  // open: en
  Multiplexer multiplexer_12 (.in0(1'b0), .in1(1'b0), .out(multiplexer_12_out), .sel(comparator_9_eq));  // open: en
  Multiplexer multiplexer_13 (.in0(1'b0), .in1(multiplexer_9_out), .out(Branch), .sel(comparator_10_gt));  // open: en
  or or_3 (Divide_by_0, multiplexer_11_out, multiplexer_12_out);
endmodule

module ShiftLeft (
  input  [15:0] A,
  input  [15:0] OUTPUT,
  input  [15:0] B
);
endmodule
